# Fritzing sketch BTHWind (saved by Fritzing 0.9.3b)

parts:
  Part1 = Lithium Ion Polymer Battery 3.7v 1200mAh [part_number=258]
  Part2 = Adafruit Feather M0 Adalogger [part_number="Adafruit #2796"]
  Part3 = Adafruit Quad AlphaNumeric Featherwing - White [part_number="Adafruit #3127"]
  Part4 = Adafruit Feather M0 RFM9x LoRa [part_number="Adafruit #3178 or #3179"]
  Part5 = 24 NeoPixel Ring [part_number=1586]
  Part6 = Adafruit_BMP280
  Part7 = Adafruit Ultimate GPS v3 [part_number="Adafruit #746"]  # not connected

nets:
  N1: Part1.positive, Part4.VBAT
  N2: Part1.negative, Part4.GND
  GND: Part2.GND, Part3.GND, Part5.GND, Part6.GND
  +3V3: Part2.+3V3, Part3.VDD, Part6.VIN
  N3: Part2.VBUS, Part3.USB, Part5.VDD
  N4: Part2.D11, Part5.IN
  N5: Part2.SCL, Part3.SCL, Part6.SCK/SCL
  N6: Part2.SDA, Part3.SDA, Part6.SDI/SDA

custom parts:
  Lithium Ion Polymer Battery 3.7v 1200mAh: Lithium ion polymer (also known as 'lipo' or 'lipoly') batteries are thin, light and powerful. The output ranges from 4.2V when completely charged to 3.7V. This battery has a capacity of 1200mAh for a total of about 4.5 Wh. The batteries come pre-attached with a genuine 2-pin JST-PH connector as shown and include the necessary protection circuitry.
  Adafruit Feather M0 Adalogger: This is the Adafruit Feather M0 Adalogger - our take on an 'all-in-one' Cortex M0 datalogger (or data-reader) with built in USB and battery charging. Its an Adafruit Feather M0 with a microSD holder ready to rock! We have other boards in the Feather family, check'em out here At the Feather M0's heart is an ATSAMD21G18 ARM Cortex M0 processor, clocked at 48 MHz and at 3.3V logic, the same one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
  Adafruit Quad AlphaNumeric Featherwing - White: This is the White Adafruit 0.54" Dual Alphanumeric Display w/ FeatherWing Combo Pack! We also have these combo packs in Green, Red, Yellow-Green, Blue, and Yellow. This is a nice, bright alphanumeric display that shows letters and numbers in a beautiful hue. It's super bright and designed for viewing from distances up to 23 feet (7 meters) away. Each of the digit sets have 14 segments on a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
  Adafruit Feather M0 RFM9x LoRa: This is the Adafruit Feather M0 RFM95 LoRa Radio - our take on an microcontroller with a "Long Range (LoRa)" packet radio transceiver with built in USB and battery charging. Its an Adafruit Feather M0 with a 433Mhz or 900MHz radio module cooked in! Great for making wireless networks that are more flexible than Bluetooth LE and without the high power requirements of WiFi. We have other boards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
  24 NeoPixel Ring: 24 ultra bright smart LED NeoPixels are arranged in a circle with 2.6" (66mm) outer diameter. The rings are 'chainable' - connect the output pin of one to the input pin of another. Use only one microcontroller pin to control as many as you can chain together! Each LED is addressable as the driver chip is inside the LED. Each one has ~18mA constant current drive so the color will be very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
  Adafruit_BMP280: Bosch has stepped up their game with their new BMP280 sensor, an environmental sensor with temperature, barometric pressure that is the next generation upgrade to the BMP085/BMP180/BMP183. This sensor is great for all sorts of weather sensing and can even be used in both I2C and SPI! This precision sensor from Bosch is the best low-cost, precision sensing solution for measuring barometric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
  Adafruit Ultimate GPS v3: We carry a few different GPS modules here in the Adafruit shop, but none that satisfied our every desire - that's why we designed this little GPS breakout board. We believe this is the Ultimate GPS module, so we named it that. It's got everything you want and more: -165 dBm sensitivity, 10 Hz updates, 66 channels 5V friendly design and only 20mA current draw Breadboard friendly + two mounting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
